// Logisim project control-logic.circ as structural Verilog: 1 circuit, main circuit control_logic
module control_logic (
  input  [31:0] Instruction,
  input  BrEq,
  input  BrLt,
  output PCSel,
  output RegWEn,
  output [2:0] ImmSel,
  output BrUn,
  output ASel,
  output BSel,
  output [3:0] ALUSel,
  output MemWEn,
  output [1:0] WBSel
);

  wire and_6_out, and_7_out, and_8_out, and_9_out, and_10_out, and_11_out, comparator_1_eq, comparator_2_eq,
       comparator_3_eq, comparator_4_eq, comparator_5_eq, comparator_6_eq, comparator_7_eq, comparator_8_eq,
       comparator_9_eq, comparator_10_eq, comparator_11_eq, comparator_12_eq, comparator_13_eq,
       comparator_14_eq, comparator_15_eq, comparator_16_eq, comparator_17_eq, comparator_18_eq,
       comparator_19_eq, comparator_20_eq, comparator_21_eq, comparator_22_eq, comparator_23_eq,
       comparator_24_eq, comparator_25_eq, comparator_26_eq, comparator_27_eq, comparator_28_eq,
       comparator_29_eq, comparator_30_eq, comparator_31_eq, comparator_32_eq, comparator_33_eq,
       comparator_34_eq, comparator_37_eq, comparator_38_eq, Imm_B, Imm_J, Imm_S, Imm_U, is_mul, is_mulh,
       is_sra, is_sub, not_1_out, not_2_out, or_1_out, or_2_out, or_7_out;
  wire [2:0] multiplexer_7_out, multiplexer_8_out, multiplexer_9_out;
  wire [3:0] multiplexer_1_out, multiplexer_2_out, multiplexer_3_out, multiplexer_5_out, RISel;
  wire [15:0] rom_1_data;

  Multiplexer #(.select(3), .width(4)) multiplexer_1 (
    .in0(4'b0000), .in1(4'b0001), .in2(4'b0010), .in3(4'b1011), .in4(4'b0100), .in5(4'b0101), .in6(4'b0110),
    .in7(4'b0111), .out(multiplexer_1_out), .sel(Instruction[14:12]));
  Multiplexer #(.width(4)) multiplexer_2 (
    .in0(multiplexer_1_out), .in1(4'b1000), .out(multiplexer_2_out), .sel(is_mul));
  Comparator #(.width(7)) comparator_1 (.a(Instruction[6:0]), .b(7'b0010011), .eq(comparator_1_eq));  // open: gt, lt
  Comparator #(.width(7)) comparator_2 (.a(Instruction[6:0]), .b(7'b0110011), .eq(comparator_2_eq));  // open: gt, lt
  Comparator #(.width(7)) comparator_3 (.a(Instruction[6:0]), .b(7'b0110011), .eq(comparator_3_eq));  // open: gt, lt
  Comparator #(.width(3)) comparator_4 (.a(Instruction[14:12]), .b(3'b000), .eq(comparator_4_eq));  // open: gt, lt
  Comparator #(.width(7)) comparator_5 (.a(Instruction[31:25]), .b(7'b0000001), .eq(comparator_5_eq));  // open: gt, lt
  Comparator #(.width(7)) comparator_6 (.a(Instruction[6:0]), .b(7'b0110011), .eq(comparator_6_eq));  // open: gt, lt
  Comparator #(.width(3)) comparator_7 (.a(Instruction[14:12]), .b(3'b000), .eq(comparator_7_eq));  // open: gt, lt
  Comparator #(.width(7)) comparator_8 (.a(Instruction[31:25]), .b(7'b0100000), .eq(comparator_8_eq));  // open: gt, lt
  Comparator #(.width(7)) comparator_9 (.a(Instruction[6:0]), .b(7'b0110011), .eq(comparator_9_eq));  // open: gt, lt
  Comparator #(.width(3)) comparator_10 (.a(Instruction[14:12]), .b(3'b001), .eq(comparator_10_eq));  // open: gt, lt
  Comparator #(.width(7)) comparator_11 (
    .a(Instruction[31:25]), .b(7'b0000001), .eq(comparator_11_eq));  // open: gt, lt
  Comparator #(.width(3)) comparator_12 (.a(Instruction[14:12]), .b(3'b101), .eq(comparator_12_eq));  // open: gt, lt
  Comparator #(.width(7)) comparator_13 (
    .a(Instruction[31:25]), .b(7'b0100000), .eq(comparator_13_eq));  // open: gt, lt
  ROM #(.addrWidth(6), .dataWidth(16)) rom_1 (.data(rom_1_data));  // open: addr
  or or_1 (or_1_out, comparator_1_eq, comparator_2_eq);
  Multiplexer #(.width(4)) multiplexer_3 (
    .in0(multiplexer_2_out), .in1(4'b1100), .out(multiplexer_3_out), .sel(is_sub));
  and and_1 (is_mul, comparator_3_eq, comparator_4_eq, comparator_5_eq);
  and and_2 (is_sub, comparator_6_eq, comparator_7_eq, comparator_8_eq);
  and and_3 (is_mulh, comparator_9_eq, comparator_10_eq, comparator_11_eq);
  and and_4 (is_sra, comparator_12_eq, comparator_13_eq);
  Multiplexer #(.width(4)) multiplexer_4 (.in0(4'b0000), .in1(RISel), .out(ALUSel), .sel(or_1_out));
  Multiplexer #(.width(4)) multiplexer_5 (
    .in0(multiplexer_3_out), .in1(4'b1001), .out(multiplexer_5_out), .sel(is_mulh));
  Multiplexer #(.width(4)) multiplexer_6 (.in0(multiplexer_5_out), .in1(4'b1101), .out(RISel), .sel(is_sra));
  Comparator #(.width(7)) comparator_14 (.a(Instruction[6:0]), .b(7'b0110011), .eq(comparator_14_eq));  // open: gt, lt
  Comparator #(.width(7)) comparator_15 (.a(Instruction[6:0]), .b(7'b0010011), .eq(comparator_15_eq));  // open: gt, lt
  Comparator #(.width(7)) comparator_16 (.a(Instruction[6:0]), .b(7'b0000011), .eq(comparator_16_eq));  // open: gt, lt
  Comparator #(.width(7)) comparator_17 (.a(Instruction[6:0]), .b(7'b1100011), .eq(comparator_17_eq));  // open: gt, lt
  Comparator #(.width(7)) comparator_18 (.a(Instruction[6:0]), .b(7'b0010111), .eq(comparator_18_eq));  // open: gt, lt
  Comparator #(.width(7)) comparator_19 (.a(Instruction[6:0]), .b(7'b1101111), .eq(comparator_19_eq));  // open: gt, lt
  Comparator #(.width(7)) comparator_20 (.a(Instruction[6:0]), .b(7'b0010011), .eq(comparator_20_eq));  // open: gt, lt
  Comparator #(.width(7)) comparator_21 (.a(Instruction[6:0]), .b(7'b0000011), .eq(comparator_21_eq));  // open: gt, lt
  Comparator #(.width(7)) comparator_22 (.a(Instruction[6:0]), .b(7'b1100011), .eq(comparator_22_eq));  // open: gt, lt
  Comparator #(.width(7)) comparator_23 (.a(Instruction[6:0]), .b(7'b1100011), .eq(comparator_23_eq));  // open: gt, lt
  Comparator #(.width(3)) comparator_24 (.a(Instruction[14:12]), .b(3'b110), .eq(comparator_24_eq));  // open: gt, lt
  Comparator #(.width(3)) comparator_25 (.a(Instruction[14:12]), .b(3'b111), .eq(comparator_25_eq));  // open: gt, lt
  or or_2 (or_2_out, comparator_24_eq, comparator_25_eq);
  or or_3 (RegWEn, comparator_14_eq, comparator_15_eq, comparator_16_eq);
  or or_4 (ASel, comparator_17_eq, comparator_18_eq, comparator_19_eq);
  or or_5 (BSel, comparator_20_eq, comparator_21_eq, comparator_22_eq);
  and and_5 (BrUn, comparator_23_eq, or_2_out);
  Multiplexer #(.width(3)) multiplexer_7 (.in0(3'b000), .in1(3'b001), .out(multiplexer_7_out), .sel(Imm_S));
  Comparator #(.width(7)) comparator_26 (.a(Instruction[6:0]), .b(7'b1100011), .eq(comparator_26_eq));  // open: gt, lt
  Comparator #(.width(3)) comparator_27 (.a(Instruction[14:12]), .b(3'b000), .eq(comparator_27_eq));  // open: gt, lt
  Comparator #(.width(3)) comparator_28 (.a(Instruction[14:12]), .b(3'b001), .eq(comparator_28_eq));  // open: gt, lt
  not not_1 (not_1_out, BrEq);
  Comparator #(.width(3)) comparator_29 (.a(Instruction[14:12]), .b(3'b100), .eq(comparator_29_eq));  // open: gt, lt
  Comparator #(.width(3)) comparator_30 (.a(Instruction[14:12]), .b(3'b110), .eq(comparator_30_eq));  // open: gt, lt
  Comparator #(.width(3)) comparator_31 (.a(Instruction[14:12]), .b(3'b101), .eq(comparator_31_eq));  // open: gt, lt
  not not_2 (not_2_out, BrLt);
  Comparator #(.width(3)) comparator_32 (.a(Instruction[14:12]), .b(3'b111), .eq(comparator_32_eq));  // open: gt, lt
  Comparator #(.width(7)) comparator_33 (.a(Instruction[6:0]), .b(7'b1101111), .eq(comparator_33_eq));  // open: gt, lt
  Comparator #(.width(7)) comparator_34 (.a(Instruction[6:0]), .b(7'b1100111), .eq(comparator_34_eq));  // open: gt, lt
  Comparator #(.width(7)) comparator_35 (.a(Instruction[6:0]), .b(7'b0100011), .eq(Imm_S));  // open: gt, lt
  Comparator #(.width(7)) comparator_36 (.a(Instruction[6:0]), .b(7'b1100011), .eq(Imm_B));  // open: gt, lt
  Comparator #(.width(7)) comparator_37 (.a(Instruction[6:0]), .b(7'b0010111), .eq(comparator_37_eq));  // open: gt, lt
  Comparator #(.width(7)) comparator_38 (.a(Instruction[6:0]), .b(7'b0110111), .eq(comparator_38_eq));  // open: gt, lt
  Comparator #(.width(7)) comparator_39 (.a(Instruction[6:0]), .b(7'b1101111), .eq(Imm_J));  // open: gt, lt
  Multiplexer #(.width(3)) multiplexer_8 (.in0(multiplexer_7_out), .in1(3'b010), .out(multiplexer_8_out), .sel(Imm_B));
  or or_6 (Imm_U, comparator_37_eq, comparator_38_eq);
  Multiplexer #(.width(3)) multiplexer_9 (.in0(multiplexer_8_out), .in1(3'b011), .out(multiplexer_9_out), .sel(Imm_U));
  and and_6 (and_6_out, comparator_26_eq, comparator_27_eq, BrEq);
  and and_7 (and_7_out, comparator_26_eq, comparator_28_eq, not_1_out);
  and and_8 (and_8_out, comparator_26_eq, comparator_29_eq, BrLt);
  and and_9 (and_9_out, comparator_26_eq, comparator_30_eq, BrLt);
  and and_10 (and_10_out, comparator_26_eq, comparator_31_eq, not_2_out);
  and and_11 (and_11_out, comparator_26_eq, comparator_32_eq, not_2_out);
  Multiplexer #(.width(3)) multiplexer_10 (.in0(multiplexer_9_out), .in1(3'b100), .out(ImmSel), .sel(Imm_J));
  or or_7 (or_7_out, and_6_out, and_7_out, and_8_out, and_9_out, and_10_out, and_11_out);
  or or_8 (PCSel, or_7_out, comparator_33_eq, comparator_34_eq);

  // Other names for the same wires on the sheet: opcode[6:0] = Instruction[6:0]; rd[4:0] = Instruction[11:7];
  //   funct3[2:0] = Instruction[14:12]; rs1[4:0] = Instruction[19:15]; rs2[4:0] = Instruction[24:20];
  //   funct7[6:0] = Instruction[31:25]

  // Notes on the sheet:
  //   Decode
  //   I Type
  //   R Type
  //   ALU Selector
  //   INPUTS to your circuit
  //   Connect ROM Input here ->
  //   ROM FOR CONTROL LOGIC
  //   DON'T CHANGE THE LOCATIONS OF THE INPUTS AND OUTPUTS!
  //   This is only if you choose to do the ROM option
  //   CONNECT
  //   WIRE
  //   TO
  //   USE
  //   ROM
  //   OUTPUT from your circuit
  //   Register Write Enable
  //   R Type
  //   I Type
  //   Ioad
  //   A Selector
  //   B Type
  //   auipc
  //   J Type
  //   B Selector
  //   I Type
  //   Ioad
  //   B Type
  //   Branch Unsign
  //   B Type
  //   bltu
  //   bgeu
  //   Reminder: If using ROM, use combinational logic for PCSel
  //   PC Selector
  //   B Type
  //   beq
  //   bne
  //   blt
  //   bltu
  //   bge
  //   bgeu
  //   J Type
  //   lui
  //   auipc
  //   lui
  //   Immediate Selector
endmodule
